# Fritzing sketch pico-project (saved by Fritzing 1.0.4)
breadboards: 1

parts:
  Mod1 = Raspberry Pi Pico W
  Grove1 = Grove OLED 128x96
  Componente1 = BME280 Breakout
  S1 = Round Pushbutton

nets:
  GND: Mod1.pin_3, Mod1.pin_8, Mod1.pin_13, Mod1.pin_18, Mod1.pin_23, Mod1.pin_28, Mod1.pin_33, Mod1.pin_38, Mod1.pin_42, Grove1.GND, Componente1.GND, S1.leg1
  N1: Mod1.pin_6, Grove1.SDA, Componente1.SDI/SDA
  N2: Mod1.pin_7, Grove1.SCL, Componente1.SCK/SCL
  N3: Mod1.pin_15, S1.leg0
  VCC: Mod1.pin_36, Grove1.VCC, Componente1.3.3V

custom parts:
  Raspberry Pi Pico W: Raspberry Pi Pico W. Based around the RP2040 microcontroller the Pico W is a low cost microcontroller device bringing Raspberry Pi quality, cost, and easy of use to the microcontroller space. The areas marked KEEPOUT in pcb silkscreen should not have traces running through them to avoid shorts on a soldered in module!
